# Fritzing sketch Esquema leitor r-fid (saved by Fritzing 0.9.1b)
breadboards: 1

parts:
  Componente1 = RFID USB Reader
  Componente2 = Arduino Leonardo (Rev3b)

nets:
  N1: Componente1.GNDT, Componente2.D10_PWM/A10
  N2: Componente1.TX-O, Componente2.GND
  N3: Componente1.GND, Componente2.RESET
  VCC: Componente1.VCC, Componente2.3V3
